# Fritzing sketch encoder_lcd_circuit (saved by Fritzing 0.9.2b)
circuit board: 9.02344cm x 10.208cm
breadboards: 1

parts:
  Part1 = Arduino Uno (Rev3)
  LCD1 = LCD screen
  U1 = POT [package=trim_pot]
  SW1 = ENCODER_RGB_CA [package=encoder_led_3]
  R1 = Resistor [tolerance=±5% resistance=100 package=THT]
  R2 = Resistor [tolerance=±5% resistance=10k package=THT]
  R3 = Resistor [tolerance=±5% resistance=220 package=THT]
  Power_plug1 = Power plug

nets:
  N1: Part1.D8, SW1.-B
  N2: Part1.D9_PWM, R1.Pin_1, R2.Pin_0
  N3: Part1.D11_PWM/MOSI, LCD1.E
  N4: Part1.D12/MISO, LCD1.RS
  GND: Part1.GND, LCD1.VSS, LCD1.R/W, U1.A, SW1.C, Power_plug1.GND
  N5: Part1.D2, LCD1.DB7
  N6: Part1.D3_PWM, LCD1.DB6
  N7: Part1.D4, LCD1.DB5
  N8: Part1.D5_PWM, LCD1.DB4
  N9: Part1.D7, SW1.+
  VIN: Part1.VIN, LCD1.VDD, U1.S, SW1.B, R2.Pin_1, R3.Pin_1, Power_plug1.VCC
  N10: LCD1.V0, U1.E
  N11: LCD1.LED+, R3.Pin_0
  N12: SW1.A, R1.Pin_0

// code stored in the sketch: encoder_lcd.ino


// include the library code:
#include <LiquidCrystal.h>

// initialize the library with the numbers of the interface pins
LiquidCrystal lcd(12, 11, 5, 4, 3, 2);

// Using a 5 pin rotary encoder made by Keyes from the 37 in 1 Sensor Kit

const int encoderPinA = 7;     // right (labeled DT on our decoder)
const int encoderPinB = 8;     // left (labeled CLK on our decoder)
const int encoderSwitchPin = 9;

volatile unsigned int encoderPos = 0;     // a counter for the dial
int buttonState = 0;

const int maxVal = 360;

// interrupt service routine vars
boolean A_set = false;
boolean B_set = false;

void doEncoderA(){
    // Test transition, did things really change?
    if( digitalRead(encoderPinA) != A_set )
    {
        A_set = !A_set;
        // adjust counter + if A leads B
        if ( A_set && !B_set )
        {
            // Increment or roll over
            if (encoderPos == maxVal)
            {
                encoderPos = 0;
            }
            else
            {
                encoderPos += 1;
            }
            
        }
    }
}

void doEncoderB(){
    if( digitalRead(encoderPinB) != B_set )
    {
        B_set = !B_set;
        //    adjust counter - 1 if B leads A
        if( B_set && !A_set )
        {
            // Decrement or roll over
            if (encoderPos == 0)
            {
              encoderPos=maxVal;
            }
            else
            {
                encoderPos -= 1;
            }
            
        }
    }
} 



void setup() {
  // set up the LCD's number of columns and rows:
  lcd.begin(16, 2);
  // Print a message to the LCD.
  lcd.print("Encoder value");
  
  pinMode(encoderPinA, INPUT_PULLUP);
pinMode(encoderPinB, INPUT_PULLUP);
pinMode(encoderSwitchPin, INPUT);

// encoder pin on interrupt 0 (pin 7)
attachInterrupt(0, doEncoderA, CHANGE);

// encoder pin on interrupt 1 (pin 8)
attachInterrupt(1, doEncoderB, CHANGE); 

}

void loop() {
  // set the cursor to column 0, line 1
  // (note: line 1 is the second row, since counting begins with 0):
  //lcd.setCursor(0, 1);
  //lcd.print("        ");
  buttonState = digitalRead(encoderSwitchPin);
  if(buttonState == LOW){
    encoderPos = 0;
  }
  lcd.setCursor(0, 1);
  // print the number of seconds since reset:
  lcd.print(encoderPos);  
  //lcd.print(buttonState); 
  lcd.print("        "); //clear following cells if neccessary
}
